# Fritzing sketch example (saved by Fritzing 0.9.3b)
breadboards: 1

parts:
  Part1 = Adafruit Si7021 Temp Humidity [part_number="Adafruit #3251"]
  Part2 = Adafruit Feather HUZZAH ESP8266 [part_number="Adafruit #2821"]

nets:
  N1: Part1.SDA, Part2.GPIO4/SDA
  N2: Part1.SCL, Part2.GPIO5/SCL
  GND: Part1.GND, Part2.GND
  VIN: Part1.VIN, Part2.3.3V

custom parts:
  Adafruit Si7021 Temp Humidity: It's summer and you're sweating and your hair's all frizzy and all you really want to know is why the weatherman said this morning that today's relative humidity would max out at a perfectly reasonable 42% when it feels more like 77%. Enter the Si7021 Temperature + Humidity Sensor - the best way to prove the weatherman wrong! This lovely sensor for Silicon labs has ± 3% relative humidity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
  Adafruit Feather HUZZAH ESP8266: his is the Adafruit Feather HUZZAH ESP8266 - our take on an 'all-in-one' ESP8266 WiFi development board with built in USB and battery charging. Its an ESP8266 WiFi module with all the extras you need, ready to rock! We have other boards in the Feather family, check'em out here. At the Feather HUZZAH's heart is an ESP8266 WiFi microcontroller clocked at 80 MHz and at 3.3V logic. This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
